// Logisim project edd31.circ as structural Verilog
module main (
  input  in_1,
  input  [15:0] data,
  input  WE,
  input  clear,
  output [15:0] out_5
);

  wire CLOCK_out;
  wire [3:0] display_unit_out_4, display_unit_out_5, display_unit_out_6, display_unit_out_7;
  wire [15:0] PC_pc;

  Program_Counter_Control PC (.PC(PC_pc));  // open: Clock, target, Halt, input, in_3
  ALU ALU ();  // open: A, Result, B, High, Operation, Zero, Negative
  Register #(.width(32)) Product_Register ();  // open: D, en, Q, clk, clr
  Clock CLOCK (.out(CLOCK_out));
  Hex_Digit_Display hex_digit_display_1 (.value(display_unit_out_4));  // open: dp
  Display_Unit_Component display_unit (
    .data(data), .WE(WE), .clear(clear), .out_4(display_unit_out_4), .out_5(display_unit_out_5),
    .out_6(display_unit_out_6), .out_7(display_unit_out_7));
  ROM #(.addrWidth(16), .dataWidth(16)) rom_1 (.addr(PC_pc), .data(out_5));  // open: sel
  Hex_Digit_Display hex_digit_display_2 (.value(display_unit_out_5));  // open: dp
  Hex_Digit_Display hex_digit_display_3 (.value(display_unit_out_6));  // open: dp
  Hex_Digit_Display hex_digit_display_4 (.value(display_unit_out_7));  // open: dp
  Register_File Register ();  // open: Write_enable, rd__write, rt__read, write_data, rs__read, rt_out, rs_out, decr7, incr7, I_type
  RAM #(.addrWidth(16), .dataWidth(16), .bus("separate")) ram_1 ();  // open: addr, din, data, str, sel, clk, ld, clr

  // Notes on the sheet:
  //   2. ROM & data
endmodule

module Display_Unit_Component (
  input  [15:0] data,
  input  WE,
  input  clear,
  output [3:0] out_4,
  output [3:0] out_5,
  output [3:0] out_6,
  output [3:0] out_7
);

  wire CLOCK;
  wire [0:0] and_1_out;
  wire [15:0] register, undriven;

  Clock u_CLOCK (.out(CLOCK));
  Multiplexer #(.select(2), .width(16), .enable("false")) multiplexer_1 (
    .in0({16{1'b0}}), .in2(data), .in3(register), .out(register), .sel({WE, and_1_out[0]}));  // open: in1
  Register #(.width(16)) register_1 (.D(register), .Q({out_7, out_6, out_5, out_4}), .clk(CLOCK));  // open: en, clr
  and and_1 (and_1_out[0], WE, clear);
  Hex_Digit_Display hex_digit_display_1 (.value(undriven[3:0]));  // open: dp
  Hex_Digit_Display hex_digit_display_2 (.value(undriven[7:4]));  // open: dp
  Hex_Digit_Display hex_digit_display_3 (.value(undriven[11:8]));  // open: dp
  Hex_Digit_Display hex_digit_display_4 (.value(undriven[15:12]));  // open: dp
endmodule

module ALU (
  input  [15:0] A,
  input  [15:0] B,
  input  [2:0] Operation,
  output [15:0] Result,
  output [15:0] High,
  output Zero,
  output Negative
);

  wire [15:0] Add, AND, Multiply, NOT, OR, SLL, SLR, Subtract;

  Adder #(.width(16)) adder_1 (.a(A), .b(B), .out(Add));  // open: cin, cout
  Subtractor #(.width(16)) subtractor_1 (.a(A), .b(B), .out(Subtract));  // open: bin, bout
  Multiplier #(.width(16)) multiplier_1 (.a(A), .b(B), .out(Multiply), .cout(High));  // open: cin
  Multiplexer #(.select(3), .width(16), .enable("false")) multiplexer_1 (
    .in0(Add), .in1(Subtract), .in2(Multiply), .in3(AND), .in4(OR), .in5(NOT), .in6(SLL), .in7(SLR),
    .out(Result), .sel(Operation));
  assign AND = A & B;  // AND_Gate AND, 16 bits wide
  assign OR = A | B;  // OR_Gate OR, 16 bits wide
  assign NOT = ~A;  // NOT_Gate not_1, 16 bits wide
  Shifter #(.width(16), .shift("lr")) shifter_1 (.in(A), .\dist (B[3:0]), .out(SLR));
  Shifter #(.width(16)) shifter_2 (.in(A), .\dist (B[3:0]), .out(SLL));
  Comparator #(.width(16)) comparator_1 (.a(Result), .b({16{1'b0}}), .eq(Zero), .lt(Negative));  // open: gt

  // Notes on the sheet:
  //   000 add
  //   001 subtract
  //   010 multiply
  //   011 AND
  //   100 OR
  //   101 NOT
  //    110 Shit Left
  //   111 8 Shift Right
  //   inputs
  //   outputs
endmodule

module Register_File (
  input  Write_enable,
  input  [2:0] rd__write,
  input  [2:0] rt__read,
  input  [15:0] write_data,
  input  [2:0] rs__read,
  input  decr7,
  input  incr7,
  input  I_type,
  output [15:0] rt_out,
  output [15:0] rs_out
);

  wire add_r7, clock, demultiplexer_1_out0, demultiplexer_1_out1, demultiplexer_1_out2, demultiplexer_1_out3,
       demultiplexer_1_out4, demultiplexer_1_out5, demultiplexer_1_out6, demultiplexer_1_out7, or_1_out,
       sub_r7;
  wire [15:0] adder_1_out, current_r7, multiplexer_2_out, register_1_q, register_2_q, register_3_q,
       register_4_q, register_5_q, register_6_q, register_7_q, subtractor_1_out;

  Clock u_clock (.out(clock));
  Demultiplexer #(.select(3), .enable("false")) demultiplexer_1 (
    .out0(demultiplexer_1_out0), .out1(demultiplexer_1_out1), .out2(demultiplexer_1_out2),
    .out3(demultiplexer_1_out3), .out4(demultiplexer_1_out4), .out5(demultiplexer_1_out5),
    .out6(demultiplexer_1_out6), .out7(demultiplexer_1_out7), .in(Write_enable), .sel(rd__write));
  Adder #(.width(16)) adder_1 (.a(current_r7), .b(16'h1), .out(adder_1_out), .cin(add_r7));  // open: cout
  Subtractor #(.width(16)) subtractor_1 (
    .a(current_r7), .b(16'h1), .out(subtractor_1_out), .bin(sub_r7));  // open: bout
  Multiplexer #(.select(2), .width(16), .enable("false")) multiplexer_1 (
    .in0(rs_out), .in1(rt_out), .out(rs_out), .sel({2{I_type}}));  // open: in2, in3
  Multiplexer #(.select(2), .width(16), .enable("false")) multiplexer_2 (
    .in0(write_data), .in1(adder_1_out), .in2(subtractor_1_out), .out(multiplexer_2_out), .sel({decr7, incr7}));  // open: in3
  or or_1 (or_1_out, demultiplexer_1_out7, decr7, incr7);
  Register #(.width(16)) register_1 (
    .D(write_data), .en(demultiplexer_1_out0), .Q(register_1_q), .clk(clock));  // open: clr
  Register #(.width(16)) register_2 (
    .D(write_data), .en(demultiplexer_1_out1), .Q(register_2_q), .clk(clock));  // open: clr
  Register #(.width(16)) register_3 (
    .D(write_data), .en(demultiplexer_1_out2), .Q(register_3_q), .clk(clock));  // open: clr
  Register #(.width(16)) register_4 (
    .D(write_data), .en(demultiplexer_1_out3), .Q(register_4_q), .clk(clock));  // open: clr
  Register #(.width(16)) register_5 (
    .D(write_data), .en(demultiplexer_1_out4), .Q(register_5_q), .clk(clock));  // open: clr
  Register #(.width(16)) register_6 (
    .D(write_data), .en(demultiplexer_1_out5), .Q(register_6_q), .clk(clock));  // open: clr
  Register #(.width(16)) register_7 (
    .D(write_data), .en(demultiplexer_1_out6), .Q(register_7_q), .clk(clock));  // open: clr
  Register #(.width(16)) r7 (.D(multiplexer_2_out), .en(or_1_out), .Q(current_r7), .clk(clock));  // open: clr
  Multiplexer #(.select(3), .width(16), .enable("false")) multiplexer_3 (
    .in0(register_1_q), .in1(register_2_q), .in2(register_3_q), .in3(register_4_q), .in4(register_5_q),
    .in5(register_6_q), .in6(register_7_q), .in7(current_r7), .out(rt_out), .sel(rt__read));
  Multiplexer #(.select(3), .width(16), .enable("false")) multiplexer_4 (
    .in0(register_1_q), .in1(register_2_q), .in2(register_3_q), .in3(register_4_q), .in4(register_5_q),
    .in5(register_6_q), .in6(register_7_q), .in7(current_r7), .out(rs_out), .sel(rs__read));

  // Other names for the same wires on the sheet: rs[2:0] = rs__read; wd[15:0] = write_data

  // Notes on the sheet:
  //   Ask Kelby about the I-type addition
endmodule

module Program_Counter_Control (
  input  Clock,
  input  [15:0] target,
  input  [7:0] in_3,
  input  Halt,
  input  [1:0] \input ,
  output [15:0] PC
);

  wire not_1_out;
  wire [15:0] adder_2_out, bit_extender_1_out, multiplexer_1_out, PC_1, PC_1_offset;

  Multiplexer #(.select(2), .width(16), .enable("false")) multiplexer_1 (
    .in0(PC_1), .in1(PC_1_offset), .in2(target), .out(multiplexer_1_out), .sel(\input ));  // open: in3
  Register #(.width(16), .trigger("falling")) u_PC (
    .D(multiplexer_1_out), .en(not_1_out), .Q(PC), .clk(Clock));  // open: clr
  not not_1 (not_1_out, Halt);
  Adder #(.width(16)) adder_1 (.a(PC), .b(16'h1), .out(PC_1));  // open: cin, cout
  Adder #(.width(16)) adder_2 (.a(PC), .b(16'h1), .out(adder_2_out));  // open: cin, cout
  assign bit_extender_1_out = {{8{in_3[7]}}, in_3};  // Bit_Extender bit_extender_1
  Adder #(.width(16)) adder_3 (.a(adder_2_out), .b(bit_extender_1_out), .out(PC_1_offset));  // open: cin, cout

  // Other names for the same wires on the sheet: offset[7:0] = in_3
endmodule
